# Fritzing sketch ESP control board (saved by Fritzing 1.0.3b)
perfboards: 1

parts:
  Header_Subwoofer = female pin header, 7 pins [form="♀ (female)"]
  Series_resistor_ST = Resistor [tolerance=±5% resistance=5,1k power=0.25W package=THT]
  NPN = NPN-Transistor [part_number=BC547B package="TO92 [THT]"]
  ESP32-WROOM32 = LuaNode32 / ESP32 [part_number=ESP32S-PIN30]
  Pull_Up = Resistor [tolerance=±5% power=0.25W resistance=100k package=THT]
  NPN1 = NPN-Transistor [part_number=BC547B package="TO92 [THT]"]
  Series_resistor_MUTE_NPN = Resistor [tolerance=±5% resistance=3,8k power=0.25W package=THT]
  PNP = PNP-Transistor [part_number=BC557B package="TO92 [THT]"]
  Series_resistor_MUTE_PNP = Resistor [tolerance=±5% resistance=5,1k power=0.25W package=THT]
  Pull_Up1 = Resistor [tolerance=±5% power=0.25W resistance=100k package=THT]
  Bauteil2 = I2C level shifter bidirectional

nets:
  5V: Header_Subwoofer.pin1, ESP32-WROOM32.Vin, Pull_Up.Pin_1, PNP.E, Pull_Up1.Pin_0, Bauteil2.HV
  GND: Header_Subwoofer.pin2, NPN.E, ESP32-WROOM32.GND, NPN1.E, Bauteil2.GND
  ST: Header_Subwoofer.pin3, NPN.C, Pull_Up.Pin_0
  MUTE: Header_Subwoofer.pin4, PNP.C
  SCL: Header_Subwoofer.pin5, Bauteil2.HV3
  SDA: Header_Subwoofer.pin6, Bauteil2.HV4
  C-D: Header_Subwoofer.pin7, Bauteil2.HV2
  N1: Series_resistor_ST.Pin_0, NPN.B
  D18: Series_resistor_ST.Pin_1, ESP32-WROOM32.D18
  3V3: ESP32-WROOM32.3V3, Bauteil2.LV
  D17: ESP32-WROOM32.TX2, Bauteil2.LV2
  D19: ESP32-WROOM32.D19, Series_resistor_MUTE_NPN.Pin_1
  D21: ESP32-WROOM32.D21, Bauteil2.LV4
  D22: ESP32-WROOM32.D22, Bauteil2.LV3
  N2: NPN1.B, Series_resistor_MUTE_NPN.Pin_0
  N3: NPN1.C, Series_resistor_MUTE_PNP.Pin_1, Pull_Up1.Pin_1
  N4: PNP.B, Series_resistor_MUTE_PNP.Pin_0

notes:
  solder
  Draht Kupfer Seite
  Draht Komponenten Seite
  Kabel Komponenten Seite

custom parts:
  LuaNode32 / ESP32: New Image for LuaNode32 DOIT ESP32 DEVKIT V1. Base parts from LuaNode32 / ESP32 ESP32 based LuaNode32 by G.Noorlander DOIT Esp32 DevKit v1 (30 pins long, 11 pins width) by Werner Rothschopf (modified by vanepp Dec 2018)
